// Logisim project Step1.circ as structural Verilog: 1 circuit, main circuit main
module main (
  input  in_1,
  input  [3:0] in_2,
  input  [7:0] in_3,
  input  [1:0] in_4,
  input  [1:0] in_5,
  input  in_6,
  input  in_7,
  output out_8,
  output [3:0] out_9,
  output [1:0] out_10,
  output [1:0] out_11,
  output [1:0] out_12,
  output [1:0] out_13,
  output [3:0] out_14,
  output [5:0] out_15,
  output [3:0] out_16,
  output [1:0] out_17,
  output [3:0] out_18,
  output [3:0] out_19,
  output [2:0] out_20,
  output [2:0] out_21
);

  wire button_1_out;

  Button button_1 (.out(button_1_out));
  // Probe on in_2
  assign out_20[1:0] = in_4 & in_5;  // AND_Gate and_1, 2 bits wide
  or or_1 (out_20[2], in_6, in_7);
  // Probe on in_2
  LED led_1 (.in(button_1_out));
  // Probe on in_2
  // Probe on in_2
  // Probe on in_2
  assign out_21 = ~out_20;  // NOT_Gate not_1, 3 bits wide

  assign out_8 = in_1;
  assign out_9 = in_2;
  assign out_10 = in_3[1:0];
  assign out_11 = in_3[3:2];
  assign out_12 = in_3[5:4];
  assign out_13 = in_3[7:6];
  assign out_14 = in_3[7:4];
  assign out_15 = in_3[7:2];
  assign out_16 = in_3[3:0];
  assign out_17 = in_3[1:0];
  assign out_18 = in_3[3:0];
  assign out_19 = in_3[7:4];
endmodule
