// Logisim project T1.circ as structural Verilog: 1 circuit, main circuit main
module main (
);

  DotMatrix #(.inputtype("row"), .matrixcols(32), .matrixrows(16)) dotmatrix_1 (
    .row0({32{1'b0}}), .row1(32'h6381ff8), .row2(32'hff381ffc), .row3(32'h7f301ff8), .row4(32'h1e301ff8),
    .row5(32'h1cf81ff8), .row6(32'h1ffc1ff8), .row7(32'h1ffe181c), .row8(32'h7ffe7ffc), .row9(32'hffb63386),
    .row10(32'hffb7ffff), .row11(32'h5f37ffff), .row12(32'h1f3707e0), .row13(32'h1e320f78),
    .row14(32'h7df03e7f), .row15(32'h79f0fc1f));
  DotMatrix #(.inputtype("row"), .matrixcols(16), .matrixrows(16)) dotmatrix_2 (
    .row0({16{1'b0}}), .row1(16'h1c1c), .row2(16'h1ffe), .row3(16'hfff8), .row4(16'hffc6), .row5(16'h1fff),
    .row6({16{1'b1}}), .row7(16'hfd98), .row8(16'hff98), .row9(16'h7f98), .row10(16'h3f38), .row11(16'h1ff8),
    .row12(16'h1838), .row13(16'h1838), .row14(16'h1ff8), .row15(16'h1ff8));
endmodule
