// Logisim project T2.circ as structural Verilog: 1 circuit, main circuit main
module main (
  input  in_1,
  input  in_2,
  input  in_3,
  input  in_4,
  input  in_5,
  input  in_6,
  input  in_7,
  input  in_8,
  input  in_9,
  input  in_10,
  input  in_11,
  input  in_12,
  input  in_13,
  input  in_14,
  input  in_15,
  input  in_16,
  input  in_17,
  input  in_18,
  input  in_19,
  input  in_20,
  input  in_21,
  input  in_22,
  input  in_23,
  input  in_24,
  input  in_25,
  input  in_26,
  input  in_27,
  input  in_28,
  input  in_29,
  input  in_30,
  input  in_31,
  input  in_32,
  input  in_33,
  input  in_34,
  input  in_35,
  input  in_36,
  input  in_37,
  input  in_38,
  input  in_39,
  input  in_40,
  input  in_41,
  input  in_42,
  input  in_43,
  input  in_44,
  input  in_45,
  input  in_46,
  input  in_47,
  input  in_48,
  input  in_49,
  input  in_50,
  input  in_51,
  input  in_52,
  input  in_53,
  input  in_54,
  input  in_55,
  input  in_56,
  input  in_57,
  input  in_58,
  input  in_59,
  input  in_60,
  input  in_61,
  input  in_62,
  input  in_63,
  input  in_64,
  input  in_65,
  input  in_66,
  input  in_67,
  input  in_68,
  input  in_69,
  input  in_70,
  input  in_71,
  input  in_72,
  input  in_73,
  input  in_74,
  input  in_75,
  input  in_76,
  input  in_77,
  input  in_78,
  input  in_79,
  input  in_80
);

  _7_Segment_Display u_7_segment_display_1 (
    .g(in_21), .f(in_1), .a(in_2), .b(in_22), .e(in_41), .d(in_61), .c(in_62), .dp(in_42));
  _7_Segment_Display u_7_segment_display_2 (
    .g(in_23), .f(in_3), .a(in_4), .b(in_24), .e(in_43), .d(in_63), .c(in_64), .dp(in_44));
  _7_Segment_Display u_7_segment_display_3 (
    .g(in_25), .f(in_5), .a(in_6), .b(in_26), .e(in_45), .d(in_65), .c(in_66), .dp(in_46));
  _7_Segment_Display u_7_segment_display_4 (
    .g(in_27), .f(in_7), .a(in_8), .b(in_28), .e(in_47), .d(in_67), .c(in_68), .dp(in_48));
  _7_Segment_Display u_7_segment_display_5 (
    .g(in_29), .f(in_9), .a(in_10), .b(in_30), .e(in_49), .d(in_69), .c(in_70), .dp(in_50));
  _7_Segment_Display u_7_segment_display_6 (
    .g(in_31), .f(in_11), .a(in_12), .b(in_32), .e(in_51), .d(in_71), .c(in_72), .dp(in_52));
  _7_Segment_Display u_7_segment_display_7 (
    .g(in_33), .f(in_13), .a(in_14), .b(in_34), .e(in_53), .d(in_73), .c(in_74), .dp(in_54));
  _7_Segment_Display u_7_segment_display_8 (
    .g(in_35), .f(in_15), .a(in_16), .b(in_36), .e(in_55), .d(in_75), .c(in_76), .dp(in_56));
  _7_Segment_Display u_7_segment_display_9 (
    .g(in_37), .f(in_17), .a(in_18), .b(in_38), .e(in_57), .d(in_77), .c(in_78), .dp(in_58));
  _7_Segment_Display u_7_segment_display_10 (
    .g(in_39), .f(in_19), .a(in_20), .b(in_40), .e(in_59), .d(in_79), .c(in_80), .dp(in_60));

  // Notes on the sheet:
  //   in_76: pull=up
  //   in_58: pull=up
  //   in_72: pull=up
  //   in_4: pull=up
  //   in_34: pull=up
  //   in_66: pull=up
  //   in_38: pull=up
  //   in_56: pull=up
  //   in_62: pull=up
  //   in_42: pull=up
  //   in_7: pull=up
  //   in_3: pull=up
  //   in_60: pull=up
  //   in_12: pull=up
  //   in_22: pull=up
  //   in_24: pull=up
  //   in_18: pull=up
  //   in_32: pull=up
  //   in_9: pull=up
  //   in_67: pull=up
  //   in_5: pull=up
  //   in_48: pull=up
  //   in_19: pull=up
  //   in_61: pull=up
  //   in_11: pull=up
  //   in_2: pull=up
  //   in_16: pull=up
  //   in_15: pull=up
  //   in_50: pull=up
  //   in_26: pull=up
  //   in_52: pull=up
  //   in_30: pull=up
  //   in_69: pull=up
  //   in_68: pull=up
  //   in_54: pull=up
  //   in_1: pull=up
  //   in_40: pull=up
  //   in_10: pull=up
  //   in_20: pull=up
  //   in_6: pull=up
  //   in_17: pull=up
  //   in_71: pull=up
  //   in_80: pull=up
  //   in_8: pull=up
  //   in_70: pull=up
  //   in_65: pull=up
  //   in_77: pull=up
  //   in_44: pull=up
  //   in_64: pull=up
  //   in_73: pull=up
  //   in_79: pull=up
  //   in_75: pull=up
  //   in_46: pull=up
  //   in_74: pull=up
  //   in_13: pull=up
  //   in_28: pull=up
  //   in_36: pull=up
  //   in_78: pull=up
  //   in_14: pull=up
  //   in_63: pull=up
endmodule
