// Logisim project T3,T4.circ as structural Verilog: 5 circuits, main circuit main
module main (
  input  [1:0] in_1,
  input  in_2,
  input  in_3,
  input  in_4,
  input  in_5,
  output out_6
);

  wire mux2_1_1_out_4, mux2_1_2_out_4;

  MUX2_1 mux2_1_1 (.in_1(in_2), .in_2(in_1[0]), .in_3(in_3), .out_4(mux2_1_1_out_4));
  MUX2_1 mux2_1_2 (.in_1(in_4), .in_2(in_1[0]), .in_3(in_5), .out_4(mux2_1_2_out_4));
  MUX2_1 mux2_1_3 (.in_1(mux2_1_1_out_4), .in_2(in_1[1]), .in_3(mux2_1_2_out_4), .out_4(out_6));
endmodule

module And (
  input  in_1,
  input  in_2,
  output out_3
);

  wire transistor_2_out;

  Transistor transistor_1 (.in(1'b0), .out(out_3), .gate(in_2));
  Transistor #(.\type ("n")) transistor_2 (.in(1'b1), .out(transistor_2_out), .gate(in_1));
  Transistor #(.\type ("n")) transistor_3 (.in(transistor_2_out), .out(out_3), .gate(in_2));
  Transistor transistor_4 (.in(1'b0), .out(out_3), .gate(in_1));
endmodule

module OR (
  input  in_1,
  input  in_2,
  output out_3
);

  wire transistor_3_out;

  Transistor #(.\type ("n")) transistor_1 (.in(1'b1), .out(out_3), .gate(in_1));
  Transistor transistor_2 (.in(transistor_3_out), .out(out_3), .gate(in_2));
  Transistor transistor_3 (.in(1'b0), .out(transistor_3_out), .gate(in_1));
  Transistor #(.\type ("n")) transistor_4 (.in(1'b1), .out(out_3), .gate(in_2));
endmodule

module NOT (
  input  in_1,
  output out_2
);

  Transistor transistor_1 (.in(1'b1), .out(out_2), .gate(in_1));
  Transistor #(.\type ("n")) transistor_2 (.in(1'b0), .out(out_2), .gate(in_1));
endmodule

module MUX2_1 (
  input  in_1,
  input  in_2,
  input  in_3,
  output out_4
);

  wire and_1_out_3, and_2_out_3, not_1_out_2;

  NOT not_1 (.in_1(in_2), .out_2(not_1_out_2));
  And and_1 (.in_1(in_1), .in_2(not_1_out_2), .out_3(and_1_out_3));
  And and_2 (.in_1(in_2), .in_2(in_3), .out_3(and_2_out_3));
  OR or_1 (.in_1(and_1_out_3), .in_2(and_2_out_3), .out_3(out_4));
endmodule
