// Logisim project Step1.circ as structural Verilog: 1 circuit, main circuit main
module main (
  input  I4,
  input  I3,
  input  I2,
  input  I1,
  output O4,
  output O3,
  output O2,
  output O1
);

  wire and_1_out, and_2_out, and_3_out, and_4_out, and_5_out, and_6_out, and_7_out, and_8_out, and_9_out,
       and_10_out, and_11_out, and_12_out, and_13_out, and_14_out, not_1_out, not_2_out, not_3_out,
       not_4_out, not_5_out, not_6_out, not_7_out, not_8_out, not_9_out, not_10_out, not_11_out, not_12_out,
       not_13_out, not_14_out, not_15_out, not_16_out, not_17_out, not_18_out, not_19_out, not_20_out,
       not_21_out;

  not not_1 (not_1_out, I4);
  and and_1 (and_1_out, not_1_out, I2, I1);
  and and_2 (and_2_out, I4, not_2_out);
  not not_2 (not_2_out, I2);
  and and_3 (and_3_out, I4, I3);
  not not_3 (not_3_out, I4);
  and and_4 (and_4_out, not_3_out, not_4_out);
  not not_4 (not_4_out, I1);
  not not_5 (not_5_out, I2);
  and and_5 (and_5_out, not_5_out, I1);
  and and_6 (and_6_out, I4, not_6_out, I2);
  not not_6 (not_6_out, I3);
  not not_7 (not_7_out, I4);
  not not_8 (not_8_out, I3);
  not not_9 (not_9_out, I2);
  not not_10 (not_10_out, I1);
  not not_11 (not_11_out, I4);
  not not_12 (not_12_out, I3);
  not not_13 (not_13_out, I3);
  not not_14 (not_14_out, I2);
  not not_15 (not_15_out, I1);
  not not_16 (not_16_out, I4);
  not not_17 (not_17_out, I3);
  not not_18 (not_18_out, I4);
  not not_19 (not_19_out, I2);
  not not_20 (not_20_out, I3);
  not not_21 (not_21_out, I1);
  or or_1 (O4, and_1_out, and_2_out, and_3_out);
  or or_2 (O3, and_4_out, and_5_out, and_6_out);
  and and_7 (and_7_out, not_7_out, not_8_out, not_9_out, not_10_out);
  and and_8 (and_8_out, not_11_out, not_12_out, I2, I1);
  and and_9 (and_9_out, I4, not_13_out, not_14_out, I1);
  and and_10 (and_10_out, I4, I3, not_15_out);
  and and_11 (and_11_out, not_16_out, not_17_out, I1);
  and and_12 (and_12_out, not_18_out, not_19_out, I1);
  and and_13 (and_13_out, I4, not_20_out, I2, not_21_out);
  and and_14 (and_14_out, I4, I3, I2, I1);
  or or_3 (O2, and_7_out, and_8_out, and_9_out, and_10_out);
  or or_4 (O1, and_11_out, and_12_out, and_13_out, and_14_out);

  // Notes on the sheet:
  //   Haozhe Sun PB20000277
endmodule
