// Logisim project Step2.circ as structural Verilog: 1 circuit, main circuit main
module main (
  input  i7,
  input  i6,
  input  i5,
  input  i4,
  input  i3,
  input  i2,
  input  i1,
  input  i0,
  output y2,
  output y1,
  output y0
);

  wire and_1_out, and_2_out, and_3_out, and_4_out, and_5_out, not_1_out, not_2_out, not_3_out, not_4_out,
       not_5_out, not_6_out, not_7_out, not_8_out, not_9_out, not_10_out;

  or or_1 (y2, i4, i5, i6, i7);
  not not_1 (not_1_out, i5);
  not not_2 (not_2_out, i4);
  and and_1 (and_1_out, not_1_out, not_2_out, i2);
  not not_3 (not_3_out, i5);
  and and_2 (and_2_out, not_3_out, not_4_out, i3);
  not not_4 (not_4_out, i4);
  not not_5 (not_5_out, i6);
  not not_6 (not_6_out, i4);
  not not_7 (not_7_out, i2);
  not not_8 (not_8_out, i6);
  not not_9 (not_9_out, i4);
  not not_10 (not_10_out, i6);
  or or_2 (y1, and_1_out, and_2_out, i6, i7);
  and and_3 (and_3_out, not_5_out, not_6_out, not_7_out, i1);
  and and_4 (and_4_out, not_8_out, not_9_out, i3);
  and and_5 (and_5_out, not_10_out, i5);
  or or_3 (y0, and_3_out, and_4_out, and_5_out, i7);

  // Notes on the sheet:
  //   Haozhe Sun PB20000277
endmodule
