// Logisim project T2.circ as structural Verilog: 1 circuit, main circuit main
module main (
  input  G1,
  input  G2,
  input  G3,
  input  A2,
  input  A1,
  input  A0,
  output Y7,
  output Y6,
  output Y5,
  output Y4,
  output Y3,
  output Y2,
  output Y1,
  output Y0
);

  wire not_1_out, not_2_out, not_3_out, not_4_out, not_5_out, not_6_out, not_7_out, not_8_out, not_9_out,
       not_10_out, not_11_out, not_12_out;

  nand nand_1 (Y7, G1, A2, A1, A0);
  not not_1 (not_1_out, A0);
  not not_2 (not_2_out, A1);
  not not_3 (not_3_out, A1);
  not not_4 (not_4_out, A0);
  not not_5 (not_5_out, A2);
  not not_6 (not_6_out, A2);
  not not_7 (not_7_out, A0);
  not not_8 (not_8_out, A2);
  not not_9 (not_9_out, A1);
  not not_10 (not_10_out, A2);
  not not_11 (not_11_out, A1);
  not not_12 (not_12_out, A0);
  nand nand_2 (Y6, G1, A2, A1, not_1_out);
  nand nand_3 (Y5, G1, A2, not_2_out, A0);
  nand nand_4 (Y4, G1, A2, not_3_out, not_4_out);
  nand nand_5 (Y3, G1, not_5_out, A1, A0);
  nand nand_6 (Y2, G1, not_6_out, A1, not_7_out);
  nand nand_7 (Y1, G1, not_8_out, not_9_out, A0);
  nand nand_8 (Y0, G1, not_10_out, not_11_out, not_12_out);

  // Notes on the sheet:
  //   Haozhe Sun PB20000277
endmodule
