// Logisim project T3,4.circ as structural Verilog: 2 circuits, main circuit Mux4-1
module Mux2_1 (
  input  a,
  input  b,
  input  c,
  output x
);

  wire and_1_out, and_2_out, not_1_out;

  not not_1 (not_1_out, b);
  and and_1 (and_1_out, a, not_1_out);
  and and_2 (and_2_out, b, c);
  or or_1 (x, and_1_out, and_2_out);
endmodule

module Mux4_1 (
  input  sel0,
  input  sel1,
  input  in_3,
  input  in_4,
  input  in_5,
  input  in_6,
  output out_7
);

  wire mux2_1_1_x, mux2_1_2_x;

  Mux2_1 mux2_1_1 (.a(in_3), .x(mux2_1_1_x), .b(sel0), .c(in_4));
  Mux2_1 mux2_1_2 (.a(in_5), .x(mux2_1_2_x), .b(sel0), .c(in_6));
  Mux2_1 mux2_1_3 (.a(mux2_1_1_x), .x(out_7), .b(sel1), .c(mux2_1_2_x));
endmodule
