// Logisim project T1.circ as structural Verilog: 1 circuit, main circuit main
module main (
  input  in_1,
  input  in_2,
  input  a,
  output out_4,
  output out_5,
  output out_6,
  output out_7,
  output out_8
);

  wire buffer_1_out, buffer_2_out, clk_out, d_ff_1_q, decoder_1_out1, decoder_1_out2, decoder_1_out3,
       decoder_2_out1, decoder_2_out2, decoder_2_out3, decoder_3_out1, decoder_3_out2, decoder_3_out3,
       multiplexer_2_out, ram_1_data;
  wire [0:0] multiplexer_1_out;

  Clock clk (.out(clk_out));
  Multiplexer multiplexer_1 (.in0(out_4), .in1(a), .out(multiplexer_1_out[0]), .sel(1'b0));  // open: en
  RAM #(.addrWidth(2), .dataWidth(1)) ram_1 (
    .addr({1'b1, multiplexer_1_out[0]}), .data(ram_1_data));  // open: sel, clk, ld, clr
  D_Flip_Flop d_ff_1 (.clk(clk_out), .D(ram_1_data), .Q(d_ff_1_q));  // open: Qn, preset, en, reset
  Multiplexer multiplexer_2 (.in0(d_ff_1_q), .in1(ram_1_data), .out(multiplexer_2_out), .sel(1'b0));  // open: en
  Decoder #(.select(2)) decoder_1 (
    .out1(decoder_1_out1), .out2(decoder_1_out2), .out3(decoder_1_out3), .sel(2'b11));  // open: out0, en
  assign out_4 = decoder_1_out1 ? in_1 : 1'bz;  // Controlled_Buffer controlled_buffer_1
  assign out_4 = decoder_1_out2 ? in_2 : 1'bz;  // Controlled_Buffer controlled_buffer_2
  assign out_4 = decoder_1_out3 ? multiplexer_2_out : 1'bz;  // Controlled_Buffer controlled_buffer_3
  assign out_5 = decoder_2_out1 ? in_1 : 1'bz;  // Controlled_Buffer controlled_buffer_4
  assign out_5 = decoder_2_out2 ? in_2 : 1'bz;  // Controlled_Buffer controlled_buffer_5
  assign out_5 = decoder_2_out3 ? multiplexer_2_out : 1'bz;  // Controlled_Buffer controlled_buffer_6
  Decoder #(.select(2)) decoder_2 (
    .out1(decoder_2_out1), .out2(decoder_2_out2), .out3(decoder_2_out3), .sel(2'b11));  // open: out0, en
  assign out_6 = decoder_3_out1 ? in_1 : 1'bz;  // Controlled_Buffer controlled_buffer_7
  Decoder #(.select(2)) decoder_3 (
    .out1(decoder_3_out1), .out2(decoder_3_out2), .out3(decoder_3_out3), .sel(2'b11));  // open: out0, en
  assign out_6 = decoder_3_out2 ? in_2 : 1'bz;  // Controlled_Buffer controlled_buffer_8
  assign out_6 = decoder_3_out3 ? multiplexer_2_out : 1'bz;  // Controlled_Buffer controlled_buffer_9
  buf buffer_1 (buffer_1_out, out_7);
  assign out_7 = 1'b1 ? out_5 : 1'bz;  // Controlled_Buffer controlled_buffer_10
  buf buffer_2 (buffer_2_out, out_8);
  assign out_8 = 1'b1 ? out_6 : 1'bz;  // Controlled_Buffer controlled_buffer_11

  // Notes on the sheet:
  //   Haozhe Sun PB20000277
endmodule
