// Logisim project T2.circ as structural Verilog: 1 circuit, main circuit main
module main (
  input  in_1,
  output [3:0] out_2
);

  wire and_1_out, and_2_out, and_3_out, and_4_out, clock_1_out, d_ff_1_q, d_ff_2_q, not_1_out, not_2_out,
       or_1_out;

  Clock clock_1 (.out(clock_1_out));
  T_Flip_Flop t_ff_1 (.clk(or_1_out), .T(1'b1), .Q(out_2[0]));  // open: Qn, preset, reset, en
  D_Flip_Flop d_ff_1 (.clk(clock_1_out), .D(in_1), .Q(d_ff_1_q));  // open: Qn, preset, en, reset
  T_Flip_Flop t_ff_2 (.clk(or_1_out), .T(out_2[0]), .Q(out_2[1]));  // open: Qn, preset, reset, en
  D_Flip_Flop d_ff_2 (.clk(clock_1_out), .D(d_ff_1_q), .Q(d_ff_2_q));  // open: Qn, preset, en, reset
  and and_1 (and_1_out, out_2[1], out_2[0]);
  not not_1 (not_1_out, d_ff_2_q);
  not not_2 (not_2_out, d_ff_1_q);
  T_Flip_Flop t_ff_3 (.clk(or_1_out), .T(and_1_out), .Q(out_2[2]));  // open: Qn, preset, reset, en
  and and_2 (and_2_out, not_1_out, d_ff_1_q);
  and and_3 (and_3_out, not_2_out, d_ff_2_q);
  T_Flip_Flop t_ff_4 (.clk(or_1_out), .T(and_4_out), .Q(out_2[3]));  // open: Qn, preset, reset, en
  and and_4 (and_4_out, out_2[2], and_1_out);
  or or_1 (or_1_out, and_2_out, and_3_out);
endmodule
